# Fritzing sketch Teensy_40_rec (saved by Fritzing 0.9.3b)
breadboards: 1

parts:
  LED1 = LED - 5mm [color="Red (633nm)" package="5 mm [THT]"]
  R1 = Resistor [tolerance=±5% resistance=220 package=THT]
  S1 = Pushbutton [package="[THT]"]
  S2 = Pushbutton [package="[THT]"]
  A1 = Teensy 4.0

nets:
  N1: LED1.cathode, S1.Pin_3, S1.Pin_4, S2.Pin_3, S2.Pin_4, A1.pin_1, A1.pin_17
  N2: LED1.anode, R1.Pin_0
  N3: R1.Pin_1, A1.pin_6
  N4: S1.Pin_1, S1.Pin_2, A1.pin_4
  N5: S2.Pin_1, S2.Pin_2, A1.pin_5

custom parts:
  Teensy 4.0: The Teensy is a complete USB-based microcontoller development system, in a very small footprint, capable of implementing many types of projects. All programming is done via the USB port. No special programmer is needed, only a standard micro-USB cable and a PC or Macintosh with a USB port. (Oct 2023 added the VBUS pad at user request.)
