# Fritzing sketch Teensy_40_rec_multipleTracks (saved by Fritzing 1.0.4)
breadboards: 1

parts:
  LED1 = LED - 5mm [color="Red (633nm)" current=0.030A package="5 mm [THT]"]
  R1 = Resistor [tolerance=±5% resistance=220 power=0.25W package=THT]
  S1 = Pushbutton [package="[THT]"]
  S2 = Pushbutton [package="[THT]"]
  A1 = Teensy 4.0
  SW1 = ENCODER_RGB_CA [package=encoder_led_3]
  S3 = Pushbutton [package="[THT]"]
  Grove1 = Grove OLED 128x96

nets:
  N1: LED1.cathode, S1.Pin_3, S1.Pin_4, S2.Pin_3, S2.Pin_4, A1.pin_1, A1.pin_17, SW1.-G, S3.Pin_3, S3.Pin_4, Grove1.GND
  N2: LED1.anode, R1.Pin_0
  N3: R1.Pin_1, A1.pin_7
  N4: S1.Pin_1, S1.Pin_2, A1.pin_4
  N5: S2.Pin_1, S2.Pin_2, A1.pin_5
  N6: A1.pin_6, S3.Pin_1, S3.Pin_2
  N7: A1.pin_11, SW1.-R
  N8: A1.pin_16, A1.pin_31, Grove1.VCC
  N9: A1.pin_25, Grove1.SDA
  N10: A1.pin_26, Grove1.SCL

custom parts:
  Teensy 4.0: The Teensy is a complete USB-based microcontoller development system, in a very small footprint, capable of implementing many types of projects. All programming is done via the USB port. No special programmer is needed, only a standard micro-USB cable and a PC or Macintosh with a USB port. (Oct 2023 added the VBUS pad at user request.)
