# Fritzing sketch recorder-speaker_diagram (saved by Fritzing 0.9.3b)
breadboards: 1

parts:
  ESP32S1 = XIAO ESP32S3(SENCE) [chip_label=ESP32S3(sense)]
  SW1 = ENCODER_RGB_CA [package=encoder_led_3]
  R1 = Resistor [tolerance=±5% resistance=1k package="2512 [SMD]"]
  S2 = Pushbutton [package="[THT]"]
  14475_SparkFun_Noisy_Cricket_Stereo_Amplifier-1_5W1 = SparkFun Noisy Cricket Stereo Amplifier - 1.5W [part_number=14475]
  SW2 = ENCODER_RGB_CA [package=encoder_led_3]  # not connected
  J1 = Piezo Speaker
  C2 = Capacitor [package=cap-pth-small2]

nets:
  N1: ESP32S1.D1, SW1.-R
  N2: ESP32S1.D3, SW1.A
  N3: ESP32S1.D6, S2.Pin_3, S2.Pin_4
  N4: ESP32S1.D7, R1.Pin_0
  3V3: ESP32S1.3V3, 14475_SparkFun_Noisy_Cricket_Stereo_Amplifier-1_5W1.VIN
  GND: ESP32S1.GND, SW1.-G, SW1.-B, S2.Pin_1, S2.Pin_2, 14475_SparkFun_Noisy_Cricket_Stereo_Amplifier-1_5W1.GND, J1.pin1, C2.2
  N5: R1.Pin_1, 14475_SparkFun_Noisy_Cricket_Stereo_Amplifier-1_5W1.RIN, 14475_SparkFun_Noisy_Cricket_Stereo_Amplifier-1_5W1.LIN, C2.1
  N6: 14475_SparkFun_Noisy_Cricket_Stereo_Amplifier-1_5W1.MONO_OUT, J1.pin2

notes:
  Power via USB-c

custom parts:
  XIAO ESP32S3(SENCE): Seeed Studio XIAO ESP32S3 leverages dual-core ESP32S3 chip, supporting both Wi-Fi and BLE wireless connectivities, which allows battery charge. It integrates built-in camera sensor, digital microphone. It offers 8MB PSRAM, 8MB FLASH, and external SD card slot. All of these make it suitable for embedded ML, like intelligent voice and vision AI.
  SparkFun Noisy Cricket Stereo Amplifier - 1.5W: You won't need a series four de-atomizer with our rendition of the Noisy Cricket, just wire it up and crank up your tunes! The Noisy Cricket Stereo Amplifier, uses the LM4853 Boomer® IC which can be configured to output up to 1.5W of power in mono operation (4Ω load) or 300mW per channel in stereo operation (8Ω load). The amplifier comes with a dual-ganged pot with a built-in switch to control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
